// Logisim project CPU_8bits.circ as structural Verilog: 11 circuits, main circuit main
module main (
  input  a7,
  input  a6,
  input  a5,
  input  a4,
  input  a3,
  input  a2,
  input  a1,
  input  a0,
  input  b7,
  input  b6,
  input  b5,
  input  b4,
  input  b3,
  input  b2,
  input  b1,
  input  b0,
  input  [2:0] _0___sumsub,
  input  _1___sub,
  input  in_19,
  output a_b,
  output a_b_2,
  output a_b_3,
  output [7:0] out_23,
  output overflow
);

  wire [3:0] binary_to_bcd_converter_1_p2, binary_to_bcd_converter_1_p3, binary_to_bcd_converter_2_p2,
       binary_to_bcd_converter_2_p3, binary_to_bcd_converter_3_p2, binary_to_bcd_converter_3_p3;
  wire [7:0] multiplexer_1_out, multiplier, sumsub;

  sumsub_8bits sumsub_8bits_1 (
    .b7(b7), .b6(b6), .a7(a7), .a6(a6), .b5(b5), .a5(a5), .b4(b4), .a4(a4), .a3(a3), .b3(b3), .a2(a2),
    .b2(b2), .a1(a1), .a0(a0), .b1(b1), .b0(b0), .sub(_1___sub), .c7(sumsub[7]), .c6(sumsub[6]),
    .c5(sumsub[5]), .c4(sumsub[4]), .c3(sumsub[3]), .c2(sumsub[2]), .c1(sumsub[1]), .c0(sumsub[0]));
  multplier_8bits multplier_8bits_1 (
    .b3(b3), .b2(b2), .b1(b1), .b0(b0), .a3(a3), .a2(a2), .a1(a1), .a0(a0), .in_9(in_19), .c7(multiplier[7]),
    .c6(multiplier[6]), .c5(multiplier[5]), .c4(multiplier[4]), .c3(multiplier[3]), .c2(multiplier[2]),
    .c1(multiplier[1]), .co(multiplier[0]));
  Multiplexer #(.select(3), .width(8)) multiplexer_1 (
    .in0(sumsub), .in1(multiplier), .in2({{5{1'b0}}, a_b_3, a_b_2, a_b}), .in3(out_23),
    .out(multiplexer_1_out), .sel(_0___sumsub));  // open: in4, in5, in6, in7
  comparador_8bits comparador_8bits_1 (
    .a0(a0), .a1(a1), .a2(a2), .a3(a3), .a4(a4), .a5(a5), .a6(a6), .a7(a7), .b0(b0), .b1(b1), .b2(b2),
    .b3(b3), .b4(b4), .b5(b5), .b6(b6), .b7(b7), .less(a_b), .equal(a_b_2), .greater(a_b_3));
  // Binary_to_BCD_converter #(.binvalue(8)) binary_to_bcd_converter_1: pin names not known; wires that end beside it: multiplexer_1_out, binary_to_bcd_converter_1_p2, binary_to_bcd_converter_1_p3
  Hex_Digit_Display #(.decimalPoint("false")) hex_digit_display_1 (.value(binary_to_bcd_converter_1_p2));
  Hex_Digit_Display #(.decimalPoint("false")) hex_digit_display_2 (.value(binary_to_bcd_converter_1_p3));
  // Binary_to_BCD_converter #(.binvalue(8)) binary_to_bcd_converter_2: pin names not known; wires that end beside it: {a7, a6, a5, a4, a3, a2, a1, a0}, binary_to_bcd_converter_2_p2, binary_to_bcd_converter_2_p3
  // Binary_to_BCD_converter #(.binvalue(8)) binary_to_bcd_converter_3: pin names not known; wires that end beside it: {b7, b6, b5, b4, b3, b2, b1, b0}, binary_to_bcd_converter_3_p2, binary_to_bcd_converter_3_p3
  Hex_Digit_Display #(.decimalPoint("false")) hex_digit_display_3 (.value(binary_to_bcd_converter_2_p2));
  Hex_Digit_Display #(.decimalPoint("false")) hex_digit_display_4 (.value(binary_to_bcd_converter_3_p2));
  Hex_Digit_Display #(.decimalPoint("false")) hex_digit_display_5 (.value(binary_to_bcd_converter_2_p3));
  Hex_Digit_Display #(.decimalPoint("false")) hex_digit_display_6 (.value(binary_to_bcd_converter_3_p3));
  bitshift bitshift_1 (.b_input({a7, a6, a5, a4, a3, a2, a1, a0}), .b_output(out_23), .cout(overflow));

  // Other names for the same wires on the sheet: bit_shift[7:0] = out_23; comparator[2:0] = {a_b_3, a_b_2, a_b};
  //   sum_or_sub = _1___sub

  // Notes on the sheet:
  //   0 = sum
  //   1 = multiplier
  //   2=comparator
  //   3=bitshift
  //   Result
  //   a value
  //   b value
endmodule

module somador_1bit (
  input  a0,
  input  a1,
  input  cin,
  output out_4,
  output out_5
);

  wire and_1_out, and_2_out, and_3_out, xor_1_out;

  xor xor_1 (xor_1_out, a0, a1);
  and and_1 (and_1_out, a0, a1);
  and and_2 (and_2_out, a0, cin);
  and and_3 (and_3_out, a1, cin);
  or or_1 (out_5, and_1_out, and_2_out, and_3_out);
  xor xor_2 (out_4, xor_1_out, cin);
endmodule

module somador_4bits (
  input  cin,
  input  b3,
  input  a3,
  input  b2,
  input  a2,
  input  b1,
  input  a1,
  input  b0,
  input  a0,
  output cout,
  output c3,
  output c2,
  output c1,
  output c0
);

  wire somador_1bit_2_out_5, somador_1bit_3_out_5, somador_1bit_4_out_5;

  somador_1bit somador_1bit_1 (.a0(a3), .a1(b3), .cin(somador_1bit_2_out_5), .out_4(c3), .out_5(cout));
  somador_1bit somador_1bit_2 (.a0(a2), .a1(b2), .cin(somador_1bit_3_out_5), .out_4(c2), .out_5(somador_1bit_2_out_5));
  somador_1bit somador_1bit_3 (.a0(a1), .a1(b1), .cin(somador_1bit_4_out_5), .out_4(c1), .out_5(somador_1bit_3_out_5));
  somador_1bit somador_1bit_4 (.a0(a0), .a1(b0), .cin(cin), .out_4(c0), .out_5(somador_1bit_4_out_5));
endmodule

module somador_8bits (
  input  cin,
  input  b7,
  input  a7,
  input  b6,
  input  a6,
  input  b5,
  input  a5,
  input  b4,
  input  a4,
  input  b3,
  input  a3,
  input  b2,
  input  a2,
  input  b1,
  input  a1,
  input  b0,
  input  a0,
  output cout,
  output c7,
  output c6,
  output c5,
  output c4,
  output c3,
  output c2,
  output c1,
  output c0
);

  wire somador_4bits_2_cout;

  somador_4bits somador_4bits_1 (
    .cin(somador_4bits_2_cout), .b3(b7), .a3(a7), .b2(b6), .a2(a6), .b1(b5), .a1(a5), .b0(b4), .a0(a4),
    .cout(cout), .c3(c7), .c2(c6), .c1(c5), .c0(c4));
  somador_4bits somador_4bits_2 (
    .cin(cin), .b3(b3), .a3(a3), .b2(b2), .a2(a2), .b1(b1), .a1(a1), .b0(b0), .a0(a0),
    .cout(somador_4bits_2_cout), .c3(c3), .c2(c2), .c1(c1), .c0(c0));
endmodule

module sumsub_8bits (
  input  b7,
  input  b6,
  input  a7,
  input  a6,
  input  b5,
  input  a5,
  input  b4,
  input  a4,
  input  a3,
  input  b3,
  input  a2,
  input  b2,
  input  a1,
  input  a0,
  input  b1,
  input  b0,
  input  sub,
  output c7,
  output c6,
  output c5,
  output c4,
  output c3,
  output c2,
  output c1,
  output c0
);

  wire bitselector_1_out, bitselector_2_out, bitselector_3_out, bitselector_4_out, bitselector_5_out,
       bitselector_6_out, bitselector_7_out, bitselector_8_out, somador_8bits_1_cout;
  wire [1:1] not_1_out, not_2_out, not_3_out, not_4_out, not_5_out, not_6_out, not_7_out, not_8_out;

  not not_1 (not_1_out[1], b7);
  not not_2 (not_2_out[1], b6);
  not not_3 (not_3_out[1], b5);
  not not_4 (not_4_out[1], b4);
  not not_5 (not_5_out[1], b3);
  not not_6 (not_6_out[1], b2);
  not not_7 (not_7_out[1], b1);
  not not_8 (not_8_out[1], b0);
  BitSelector #(.width(2)) bitselector_1 (.in({not_1_out[1], b7}), .out(bitselector_1_out), .sel(sub));
  BitSelector #(.width(2)) bitselector_2 (.in({not_2_out[1], b6}), .out(bitselector_2_out), .sel(sub));
  BitSelector #(.width(2)) bitselector_3 (.in({not_3_out[1], b5}), .out(bitselector_3_out), .sel(sub));
  BitSelector #(.width(2)) bitselector_4 (.in({not_4_out[1], b4}), .out(bitselector_4_out), .sel(sub));
  BitSelector #(.width(2)) bitselector_5 (.in({not_5_out[1], b3}), .out(bitselector_5_out), .sel(sub));
  BitSelector #(.width(2)) bitselector_6 (.in({not_6_out[1], b2}), .out(bitselector_6_out), .sel(sub));
  BitSelector #(.width(2)) bitselector_7 (.in({not_7_out[1], b1}), .out(bitselector_7_out), .sel(sub));
  BitSelector #(.width(2)) bitselector_8 (.in({not_8_out[1], b0}), .out(bitselector_8_out), .sel(sub));
  somador_8bits somador_8bits_1 (
    .cin(sub), .b7(bitselector_1_out), .a7(a7), .b6(bitselector_2_out), .a6(a6), .b5(bitselector_3_out),
    .a5(a5), .b4(bitselector_4_out), .a4(a4), .b3(bitselector_5_out), .a3(a3), .b2(bitselector_6_out),
    .a2(a2), .b1(bitselector_7_out), .a1(a1), .b0(bitselector_8_out), .a0(a0), .cout(somador_8bits_1_cout),
    .c7(c7), .c6(c6), .c5(c5), .c4(c4), .c3(c3), .c2(c2), .c1(c1), .c0(c0));
endmodule

module comparador_1bit (
  input  a,
  input  b,
  output greater,
  output equal,
  output less
);

  wire not_1_out, not_2_out;

  not not_1 (not_1_out, b);
  not not_2 (not_2_out, a);
  and and_1 (greater, a, not_1_out);
  and and_2 (less, not_2_out, b);
  nor nor_1 (equal, greater, less);
endmodule

module comparador_2bits (
  input  a0,
  input  b0,
  input  a1,
  input  b1,
  output less,
  output equal,
  output greater
);

  wire and_1_out, and_3_out, comparador_1bit_1_equal, comparador_1bit_1_greater, comparador_1bit_1_less,
       comparador_1bit_2_equal, comparador_1bit_2_greater, comparador_1bit_2_less;

  and and_1 (and_1_out, comparador_1bit_1_less, comparador_1bit_2_equal);
  or or_1 (less, and_1_out, comparador_1bit_2_less);
  comparador_1bit comparador_1bit_1 (
    .a(a0), .b(b0), .greater(comparador_1bit_1_greater), .equal(comparador_1bit_1_equal),
    .less(comparador_1bit_1_less));
  and and_2 (equal, comparador_1bit_1_equal, comparador_1bit_2_equal);
  comparador_1bit comparador_1bit_2 (
    .a(a1), .b(b1), .greater(comparador_1bit_2_greater), .equal(comparador_1bit_2_equal),
    .less(comparador_1bit_2_less));
  or or_2 (greater, comparador_1bit_2_greater, and_3_out);
  and and_3 (and_3_out, comparador_1bit_1_greater, comparador_1bit_2_equal);
endmodule

module comparador_4bits (
  input  a0,
  input  a1,
  input  a2,
  input  a3,
  input  b0,
  input  b1,
  input  b2,
  input  b3,
  output less,
  output equal,
  output greater
);

  wire and_1_out, and_3_out, comparador_2bits_1_equal, comparador_2bits_1_greater, comparador_2bits_1_less,
       comparador_2bits_2_equal, comparador_2bits_2_greater, comparador_2bits_2_less;

  or or_1 (less, and_1_out, comparador_2bits_2_less);
  and and_1 (and_1_out, comparador_2bits_1_less, comparador_2bits_2_equal);
  comparador_2bits comparador_2bits_1 (
    .a0(a0), .b0(b0), .a1(a1), .b1(b1), .less(comparador_2bits_1_less), .equal(comparador_2bits_1_equal),
    .greater(comparador_2bits_1_greater));
  and and_2 (equal, comparador_2bits_1_equal, comparador_2bits_2_equal);
  comparador_2bits comparador_2bits_2 (
    .a0(a2), .b0(b2), .a1(a3), .b1(b3), .less(comparador_2bits_2_less), .equal(comparador_2bits_2_equal),
    .greater(comparador_2bits_2_greater));
  or or_2 (greater, comparador_2bits_2_greater, and_3_out);
  and and_3 (and_3_out, comparador_2bits_2_equal, comparador_2bits_1_greater);
endmodule

module comparador_8bits (
  input  a0,
  input  a1,
  input  a2,
  input  a3,
  input  a4,
  input  a5,
  input  a6,
  input  a7,
  input  b0,
  input  b1,
  input  b2,
  input  b3,
  input  b4,
  input  b5,
  input  b6,
  input  b7,
  output less,
  output equal,
  output greater
);

  wire and_1_out, and_3_out, comparador_4bits_1_equal, comparador_4bits_1_greater, comparador_4bits_1_less,
       comparador_4bits_2_equal, comparador_4bits_2_greater, comparador_4bits_2_less;

  or or_1 (less, and_1_out, comparador_4bits_2_less);
  and and_1 (and_1_out, comparador_4bits_1_less, comparador_4bits_2_equal);
  comparador_4bits comparador_4bits_1 (
    .a0(a0), .a1(a1), .a2(a2), .a3(a3), .b0(b0), .b1(b1), .b2(b2), .b3(b3), .less(comparador_4bits_1_less),
    .equal(comparador_4bits_1_equal), .greater(comparador_4bits_1_greater));
  and and_2 (equal, comparador_4bits_1_equal, comparador_4bits_2_equal);
  comparador_4bits comparador_4bits_2 (
    .a0(a4), .a1(a5), .a2(a6), .a3(a7), .b0(b4), .b1(b5), .b2(b6), .b3(b7), .less(comparador_4bits_2_less),
    .equal(comparador_4bits_2_equal), .greater(comparador_4bits_2_greater));
  or or_2 (greater, comparador_4bits_2_greater, and_3_out);
  and and_3 (and_3_out, comparador_4bits_1_greater, comparador_4bits_2_equal);
endmodule

module bitshift (
  input  [7:0] b_input,
  output [7:0] b_output,
  output cout
);


  assign b_output = {b_input[6:0], 1'b0};
  assign cout = b_input[7];
endmodule

module multplier_8bits (
  input  b3,
  input  b2,
  input  b1,
  input  b0,
  input  a3,
  input  a2,
  input  a1,
  input  a0,
  input  in_9,
  output c7,
  output c6,
  output c5,
  output c4,
  output c3,
  output c2,
  output c1,
  output co
);

  wire [2:0] and_15_out;
  wire [3:0] adder_2_cout, and_4_out, and_8_out, and_12_out;
  wire [3:1] adder_3_out;
  wire [3:3] adder_3_cout;

  and and_1 (and_4_out[3], a3, b3);
  and and_2 (and_4_out[2], a3, b2);
  and and_3 (and_4_out[1], a3, b1);
  and and_4 (and_4_out[0], a3, b0);
  and and_5 (and_8_out[3], a2, b3);
  and and_6 (and_8_out[2], a2, b2);
  and and_7 (and_8_out[1], a2, b1);
  and and_8 (and_8_out[0], a2, b0);
  Adder #(.width(4)) adder_1 (.a(adder_2_cout), .b(and_4_out), .out({c6, c5, c4, c3}), .cout(c7));  // open: cin
  and and_9 (and_12_out[3], a1, b3);
  and and_10 (and_12_out[2], a1, b2);
  and and_11 (and_12_out[1], a1, b1);
  Adder #(.width(4)) adder_2 (
    .a({adder_3_cout[3], adder_3_out}), .b(and_8_out), .out({adder_2_cout[2:0], c2}), .cout(adder_2_cout[3]));  // open: cin
  and and_12 (and_12_out[0], a1, b0);
  and and_13 (and_15_out[2], a0, b3);
  Adder #(.width(4)) adder_3 (
    .a({in_9, and_15_out}), .b(and_12_out), .out({adder_3_out, c1}), .cout(adder_3_cout[3]));  // open: cin
  and and_14 (and_15_out[1], a0, b2);
  and and_15 (and_15_out[0], a0, b1);
  and and_16 (co, a0, b0);
endmodule
